// Logisim project 658_Computer.circ as structural Verilog: 1 circuit, main circuit main
module main (
);

  wire A_128K_B, and_2_out, and_3_out, and_7_out, BA0_3_LOW, BA4_7_LOW, clock_2_out, DEVICE, ds1813_1_p2,
       IRAM_A17, IRQ_B, IRQ_V, NMI_B, not_1_out, not_2_out, not_3_out, not_4_out, not_5_out, not_6_out,
       not_7_out, not_8_out, not_9_out, not_10_out, not_11_out, not_12_out, or_1_out, or_2_out, PHI2,
       pull_resistor_1_node, pull_resistor_3_node, pull_resistor_4_node, pull_resistor_5_node,
       pull_resistor_6_node, pull_resistor_8_node, RWB, VA_B, VDA, VP_B, VPA, w65c816_1_p7, w65c816_1_p11;
  wire [2:0] ls148_1_p3;
  wire [3:0] A0_3;
  wire [7:0] A8_15, BA0_7, D, IRAM_A0_7, IRAM_A8_16;
  wire [7:1] lvc164245_1_p8;
  wire [7:4] A0_7;
  wire [7:7] pull_resistor_7_node;

  Clock clock_1 (.out(PHI2));
  Clock clock_2 (.out(clock_2_out));
  // DS1813 ds1813_1: pin names not known; wires that end beside it: clock_2_out, ds1813_1_p2
  Pull_Resistor #(.pull(1)) pull_resistor_1 (.node(pull_resistor_1_node));
  and and_1 (VA_B, ~VDA, ~VPA);  // AND_Gate
  not not_1 (not_1_out, BA0_7[0]);
  not not_2 (not_2_out, BA0_7[1]);
  not not_3 (not_3_out, BA0_7[2]);
  not not_4 (not_4_out, BA0_7[3]);
  not not_5 (not_5_out, BA0_7[4]);
  not not_6 (not_6_out, BA0_7[5]);
  not not_7 (not_7_out, BA0_7[6]);
  not not_8 (not_8_out, BA0_7[7]);
  and and_2 (and_2_out, A8_15[4], A8_15[5], A8_15[6], A8_15[7]);
  and and_3 (and_3_out, not_2_out, not_3_out, not_4_out);
  and and_4 (BA0_3_LOW, not_1_out, not_2_out, not_3_out, not_4_out);
  and and_5 (BA4_7_LOW, not_5_out, not_6_out, not_7_out, not_8_out);
  and and_6 (DEVICE, ~A8_15[3], and_2_out, BA0_3_LOW, BA4_7_LOW);  // AND_Gate
  // W65C816 w65c816_1: pin names not known; wires that end beside it: pull_resistor_1_node, IRQ_B, NMI_B, ds1813_1_p2, PHI2, {A8_15, A0_7, A0_3}, w65c816_1_p7, RWB, VDA, VPA, w65c816_1_p11, VP_B
  nand nand_1 (A_128K_B, and_3_out, BA4_7_LOW);
  // Probe on {A8_15, A0_7, A0_3}
  // Probe on w65c816_1_p7
  Pull_Resistor #(.pull(1)) pull_resistor_2 (.node(w65c816_1_p11));
  or or_1 (or_1_out, VA_B, DEVICE, A_128K_B, IRQ_V);
  or or_2 (or_2_out, DEVICE, A_128K_B, VA_B);
  Pull_Resistor pull_resistor_3 (.node(pull_resistor_3_node));
  Pull_Resistor pull_resistor_4 (.node(pull_resistor_4_node));
  not not_9 (not_9_out, PHI2);
  not not_10 (not_10_out, PHI2);
  Pull_Resistor pull_resistor_5 (.node(pull_resistor_5_node));
  // LVC573 lvc573_1: pin names not known; wires that end beside it: pull_resistor_4_node, w65c816_1_p7, not_9_out, BA0_7
  // LVC4245 lvc4245_1: pin names not known; wires that end beside it: not_10_out, w65c816_1_p7, RWB, D
  // LVC4245 lvc4245_2: pin names not known; wires that end beside it: or_1_out, {A0_7, A0_3}, pull_resistor_3_node, IRAM_A0_7
  // LVC164245 lvc164245_1: pin names not known; wires that end beside it: or_2_out, or_2_out, A8_15, pull_resistor_5_node, BA0_7, pull_resistor_5_node, IRAM_A8_16, {lvc164245_1_p8, IRAM_A17}
  // Probe on BA0_7
  // Probe on D
  Pull_Resistor pull_resistor_6 (.node(pull_resistor_6_node));
  // LS148 ls148_1: pin names not known; wires that end beside it: pull_resistor_6_node, {8{1'b1}}, ls148_1_p3, IRQ_B
  // Probe on {IRAM_A17, IRAM_A8_16, IRAM_A0_7}
  RAM #(.addrWidth(17), .databus("bidir"), .enables("line"), .trigger("high"), .\type ("nonvolatile")) ram_1 (
    .addr({IRAM_A17, IRAM_A8_16, IRAM_A0_7}), .data(D));  // open: we, oe, clk
  not not_11 (not_11_out, RWB);
  Pull_Resistor pull_resistor_7 (.node(pull_resistor_7_node[7]));
  and and_7 (and_7_out, A0_3[1], A0_3[2], A0_3[3], ~VP_B);  // AND_Gate
  not not_12 (not_12_out, IRQ_V);
  // Probe on {{4{pull_resistor_7_node[7]}}, ls148_1_p3, A0_3[0]}
  and and_8 (IRQ_V, and_7_out, ~IRQ_B);  // AND_Gate
  Pull_Resistor pull_resistor_8 (.node(pull_resistor_8_node));
  // Probe on D
  // LVC4245 lvc4245_3: pin names not known; wires that end beside it: not_12_out, {{4{pull_resistor_7_node[7]}}, ls148_1_p3, A0_3[0]}, pull_resistor_8_node, IRAM_A0_7
  Pull_Resistor #(.pull(1)) pull_resistor_9 (.node(NMI_B));
  // Probe on IRAM_A0_7

  // Other names for the same wires on the sheet: A0_7[3:0] = A0_3; A4_7[3:0] = A0_7

  // Notes on the sheet:
  //   Valid Address
  //   Bank Decode
  //   Device Decode
endmodule
